// Digital circuit counter.dig as structural Verilog
module counter (
  input  SET,
  input  X,
  output I_0,
  output I_1
);

  wire d_ff_as_1_nq, d_ff_as_2_nq;

  D_FF_AS d_ff_as_1 (.Set(1'b0), .D(d_ff_as_1_nq), .C(X), .Clr(1'b0), .Q(I_0), .nQ(d_ff_as_1_nq));
  D_FF_AS d_ff_as_2 (.Set(1'b0), .D(d_ff_as_2_nq), .C(d_ff_as_1_nq), .Clr(SET), .Q(I_1), .nQ(d_ff_as_2_nq));
endmodule
