// Digital circuit project.dig as structural Verilog
module project (
  input  clk
);

  wire counter_1_i_0, counter_1_i_1, not_1_out, not_2_out, S_out, seq_minimized_1_la, seq_minimized_1_lb,
       seq_minimized_1_lc, seq_minimized_1_ld, seq_minimized_1_le, X_out;

  Button X (.out(X_out));
  Button S (.out(S_out));
  counter counter_1 (.SET(S_out), .X(X_out), .I_0(counter_1_i_0), .I_1(counter_1_i_1));
  seq_minimized seq_minimized_1 (
    .C(clk), .I_0(counter_1_i_0), .nI_0(not_1_out), .I_1(counter_1_i_1), .nI_1(not_2_out), .S(S_out),
    .LA(seq_minimized_1_la), .LB(seq_minimized_1_lb), .LC(seq_minimized_1_lc), .LD(seq_minimized_1_ld),
    .LE(seq_minimized_1_le));
  not not_1 (not_1_out, counter_1_i_0);
  not not_2 (not_2_out, counter_1_i_1);
  LED led_1 (.in(seq_minimized_1_la));
  LED led_2 (.in(seq_minimized_1_lb));
  LED led_3 (.in(seq_minimized_1_lc));
  LED led_4 (.in(seq_minimized_1_ld));
  LED led_5 (.in(seq_minimized_1_le));

  // Notes on the sheet:
  //   clk: Hz: 2
endmodule
