// Digital circuit seq_minimized.dig as structural Verilog
module seq_minimized (
  input  C,
  input  I_0,
  input  nI_0,
  input  I_1,
  input  nI_1,
  input  S,
  output LA,
  output LB,
  output LC,
  output LD,
  output LE
);

  wire and_1_out, and_2_out, and_3_out, and_4_out, and_5_out, and_6_out, and_7_out, and_8_out, and_9_out,
       and_10_out, and_11_out, and_12_out, and_13_out, and_14_out, and_15_out, and_16_out, and_17_out,
       and_18_out, and_19_out, and_20_out, not_1_out, not_2_out, not_3_out, not_4_out, or_1_out, or_2_out,
       or_3_out, or_4_out, or_5_out, or_7_out, or_8_out, Q_0, Q_1, Q_2, Q_3, Q_4;

  and and_1 (and_1_out, nI_1, nI_0);
  and and_2 (and_2_out, nI_1, I_0);
  and and_3 (and_3_out, I_1, nI_0);
  and and_4 (and_4_out, I_1, I_0);
  not not_1 (not_1_out, and_4_out);
  not not_2 (not_2_out, and_2_out);
  not not_3 (not_3_out, and_1_out);
  not not_4 (not_4_out, and_3_out);
  and and_5 (and_5_out, Q_0, not_1_out);
  and and_6 (and_6_out, Q_2, and_4_out);
  or or_1 (or_1_out, Q_3, Q_4);
  and and_7 (and_7_out, Q_1, not_2_out);
  and and_8 (and_8_out, Q_2, and_2_out);
  and and_9 (and_9_out, Q_3, and_4_out);
  and and_10 (and_10_out, Q_0, and_4_out);
  and and_11 (and_11_out, Q_2, nI_0);
  and and_12 (and_12_out, Q_3, and_3_out);
  and and_13 (and_13_out, Q_4, not_3_out);
  and and_14 (and_14_out, Q_1, I_1);
  and and_15 (and_15_out, Q_3, not_4_out);
  and and_16 (and_16_out, Q_0, and_3_out);
  and and_17 (and_17_out, Q_1, and_2_out);
  and and_18 (and_18_out, Q_2, and_4_out);
  and and_19 (and_19_out, Q_4, nI_0);
  or or_2 (or_2_out, and_5_out, and_6_out);
  and and_20 (and_20_out, or_1_out, and_3_out);
  or or_3 (or_3_out, and_7_out, and_8_out);
  or or_4 (or_4_out, and_10_out, and_11_out);
  or or_5 (or_5_out, and_12_out, and_13_out);
  or or_6 (LD, and_14_out, and_15_out);
  or or_7 (or_7_out, and_16_out, and_17_out);
  or or_8 (or_8_out, and_18_out, and_19_out);
  or or_9 (LA, or_2_out, and_20_out);
  or or_10 (LB, or_3_out, and_9_out);
  or or_11 (LC, or_4_out, or_5_out);
  or or_12 (LE, or_7_out, or_8_out);
  // Probe on LA
  // Probe on LB
  // Probe on LC
  // Probe on LD
  // Probe on LE
  // Probe on Q_0
  // Probe on Q_1
  // Probe on Q_2
  // Probe on Q_3
  // Probe on Q_4
  D_FF_AS D_0 (.Set(S), .D(Q_4), .C(C), .Clr(1'b0), .Q(Q_0));  // open: nQ
  D_FF_AS D_1 (.Set(1'b0), .D(Q_0), .C(C), .Clr(S), .Q(Q_1));  // open: nQ
  D_FF_AS D_2 (.Set(1'b0), .D(Q_1), .C(C), .Clr(S), .Q(Q_2));  // open: nQ
  D_FF_AS D_3 (.Set(1'b0), .D(Q_2), .C(C), .Clr(S), .Q(Q_3));  // open: nQ
  D_FF_AS D_4 (.Set(1'b0), .D(Q_3), .C(C), .Clr(S), .Q(Q_4));  // open: nQ

  // Notes on the sheet:
  //   ~I_1~I_0
  //   ~I_{1}I_0
  //   I_1~I_0
  //   I_{1}I_0
endmodule
